# Fritzing sketch aitostart (saved by Fritzing 0.9.3b)
breadboards: 1

parts:
  Часть1 = Arduino Nano (Rev3.0)
  LM1 = RioRand LM2596
  SIM800L_BO1 = SIM800L BO
  U1 = 4-Channel 5v Relay Shield [package=relay-4ch5v10a]
  Power_plug1 = Power plug
  DS1 = DS18B20 1-Wire Temperature Sensor [part_number=DS18B20]
  R1 = Resistor [tolerance=±5% resistance=10k package=THT]
  R2 = Resistor [tolerance=±5% resistance=10k package=THT]

nets:
  GND: Часть1.GND, U1.GND, Power_plug1.GND, DS1.DQ, R2.Pin_1
  N1: Часть1.D2, DS1.GND
  N2: Часть1.D3, SIM800L_BO1.pin_5
  N3: Часть1.D4, R1.Pin_0
  N4: Часть1.D5, U1.IN4
  N5: Часть1.D6, U1.IN3
  N6: Часть1.D7, U1.IN2
  N7: Часть1.D8, U1.IN1
  VCC: Часть1.VIN, U1.VCC, Power_plug1.VCC
  3V3: Часть1.3V3, DS1.VDD
  N8: LM1.Pin_2, SIM800L_BO1.PIN2
  N9: LM1.Pin_3, SIM800L_BO1.pin_6
  N10: SIM800L_BO1.pin_4, R1.Pin_1, R2.Pin_0

custom parts:
  4-Channel 5v Relay Shield: 4 Channel 5v Relay Shield w. 2x SPD-06VDC-SD-C
